// Logisim project main.circ as structural Verilog: 16 circuits, main circuit main
module main (
  input  [31:0] in_1,
  input  [31:0] in_2,
  input  [31:0] in_3,
  input  [31:0] in_4,
  input  [31:0] in_5,
  input  [31:0] in_6,
  input  [31:0] in_7,
  input  [31:0] in_8,
  input  [31:0] in_9,
  input  [31:0] Load_sample,
  input  [5:0] x,
  input  [5:0] y,
  input  state,
  input  Load_to_MR1,
  input  Load_to__MR2
);

  wire clk, n32bit_decoder_short_1_dot, n32bit_decoder_short_1_sign, n32bit_decoder_short_2_dot,
       n32bit_decoder_short_2_sign, n32bit_decoder_short_3_dot, n32bit_decoder_short_3_sign,
       n32bit_decoder_short_4_dot, n32bit_decoder_short_4_sign, n32bit_decoder_short_5_dot,
       n32bit_decoder_short_5_sign, n32bit_decoder_short_6_dot, n32bit_decoder_short_6_sign,
       n32bit_decoder_short_7_dot, n32bit_decoder_short_7_sign, n32bit_decoder_short_8_dot,
       n32bit_decoder_short_8_sign, n32bit_decoder_short_9_dot, n32bit_decoder_short_9_sign, reset_out,
       update_out;
  wire [3:0] n32bit_decoder_short_1__0, n32bit_decoder_short_1__1, n32bit_decoder_short_1__1_2,
       n32bit_decoder_short_1__2, n32bit_decoder_short_1__2_2, n32bit_decoder_short_1__3,
       n32bit_decoder_short_1__3_2, n32bit_decoder_short_1__4, n32bit_decoder_short_1__4_2,
       n32bit_decoder_short_1__5, n32bit_decoder_short_2__0, n32bit_decoder_short_2__1,
       n32bit_decoder_short_2__1_2, n32bit_decoder_short_2__2, n32bit_decoder_short_2__2_2,
       n32bit_decoder_short_2__3, n32bit_decoder_short_2__3_2, n32bit_decoder_short_2__4,
       n32bit_decoder_short_2__4_2, n32bit_decoder_short_2__5, n32bit_decoder_short_3__0,
       n32bit_decoder_short_3__1, n32bit_decoder_short_3__1_2, n32bit_decoder_short_3__2,
       n32bit_decoder_short_3__2_2, n32bit_decoder_short_3__3, n32bit_decoder_short_3__3_2,
       n32bit_decoder_short_3__4, n32bit_decoder_short_3__4_2, n32bit_decoder_short_3__5,
       n32bit_decoder_short_4__0, n32bit_decoder_short_4__1, n32bit_decoder_short_4__1_2,
       n32bit_decoder_short_4__2, n32bit_decoder_short_4__2_2, n32bit_decoder_short_4__3,
       n32bit_decoder_short_4__3_2, n32bit_decoder_short_4__4, n32bit_decoder_short_4__4_2,
       n32bit_decoder_short_4__5, n32bit_decoder_short_5__0, n32bit_decoder_short_5__1,
       n32bit_decoder_short_5__1_2, n32bit_decoder_short_5__2, n32bit_decoder_short_5__2_2,
       n32bit_decoder_short_5__3, n32bit_decoder_short_5__3_2, n32bit_decoder_short_5__4,
       n32bit_decoder_short_5__4_2, n32bit_decoder_short_5__5, n32bit_decoder_short_6__0,
       n32bit_decoder_short_6__1, n32bit_decoder_short_6__1_2, n32bit_decoder_short_6__2,
       n32bit_decoder_short_6__2_2, n32bit_decoder_short_6__3, n32bit_decoder_short_6__3_2,
       n32bit_decoder_short_6__4, n32bit_decoder_short_6__4_2, n32bit_decoder_short_6__5,
       n32bit_decoder_short_7__0, n32bit_decoder_short_7__1, n32bit_decoder_short_7__1_2,
       n32bit_decoder_short_7__2, n32bit_decoder_short_7__2_2, n32bit_decoder_short_7__3,
       n32bit_decoder_short_7__3_2, n32bit_decoder_short_7__4, n32bit_decoder_short_7__4_2,
       n32bit_decoder_short_7__5, n32bit_decoder_short_8__0, n32bit_decoder_short_8__1,
       n32bit_decoder_short_8__1_2, n32bit_decoder_short_8__2, n32bit_decoder_short_8__2_2,
       n32bit_decoder_short_8__3, n32bit_decoder_short_8__3_2, n32bit_decoder_short_8__4,
       n32bit_decoder_short_8__4_2, n32bit_decoder_short_8__5, n32bit_decoder_short_9__0,
       n32bit_decoder_short_9__1, n32bit_decoder_short_9__1_2, n32bit_decoder_short_9__2,
       n32bit_decoder_short_9__2_2, n32bit_decoder_short_9__3, n32bit_decoder_short_9__3_2,
       n32bit_decoder_short_9__4, n32bit_decoder_short_9__4_2, n32bit_decoder_short_9__5;
  wire [31:0] _11, _12, _13, _21, _22, _23, _31, _32, _33, dotmatrix_1_p1, dotmatrix_1_p2,
       matrix_reg_rev_1_out_11, matrix_reg_rev_1_out_12, matrix_reg_rev_1_out_13, matrix_reg_rev_1_out_21,
       matrix_reg_rev_1_out_22, matrix_reg_rev_1_out_23, matrix_reg_rev_1_out_31, matrix_reg_rev_1_out_32,
       matrix_reg_rev_1_out_33, matrix_reg_rev_2_out_11, matrix_reg_rev_2_out_12, matrix_reg_rev_2_out_13,
       matrix_reg_rev_2_out_21, matrix_reg_rev_2_out_22, matrix_reg_rev_2_out_23, matrix_reg_rev_2_out_31,
       matrix_reg_rev_2_out_32, matrix_reg_rev_2_out_33, n64x64_display_controller_1_x12,
       n64x64_display_controller_1_x21, n64x64_display_controller_1_x22, n64x64_display_controller_1_y12,
       n64x64_display_controller_1_y21, n64x64_display_controller_1_y22, R1_11, R1_12, R1_13, R1_21, R1_22,
       R1_23, R1_31, R1_32, R1_33, R2_11, R2_12, R2_13, R2_21, R2_22, R2_23, R2_31, R2_32, R2_33;

  Clock clock_1 (.out(clk));
  ROM #(.dataWidth(32)) rom_1 ();  // open: addr, data, sel
  ROM #(.dataWidth(32)) rom_2 ();  // open: addr, data, sel
  _7_Segment_Display u_7_segment_display_1 (.g(n32bit_decoder_short_1_sign));  // open: f, a, b, e, d, c, dp
  _32bit_decoder_short u_32bit_decoder_short_1 (
    .sign(n32bit_decoder_short_1_sign), ._4(n32bit_decoder_short_1__4), ._3(n32bit_decoder_short_1__3),
    ._2_2(n32bit_decoder_short_1__2_2), ._1_2(n32bit_decoder_short_1__1_2), ._0(n32bit_decoder_short_1__0),
    .dot(n32bit_decoder_short_1_dot), .in(_11), ._1(n32bit_decoder_short_1__1),
    ._2(n32bit_decoder_short_1__2), ._3_2(n32bit_decoder_short_1__3_2), ._4_2(n32bit_decoder_short_1__4_2),
    ._5(n32bit_decoder_short_1__5));
  _7_Segment_Display u_7_segment_display_2 (.g(n32bit_decoder_short_2_sign));  // open: f, a, b, e, d, c, dp
  _32bit_decoder_short u_32bit_decoder_short_2 (
    .sign(n32bit_decoder_short_2_sign), ._4(n32bit_decoder_short_2__4), ._3(n32bit_decoder_short_2__3),
    ._2_2(n32bit_decoder_short_2__2_2), ._1_2(n32bit_decoder_short_2__1_2), ._0(n32bit_decoder_short_2__0),
    .dot(n32bit_decoder_short_2_dot), .in(_12), ._1(n32bit_decoder_short_2__1),
    ._2(n32bit_decoder_short_2__2), ._3_2(n32bit_decoder_short_2__3_2), ._4_2(n32bit_decoder_short_2__4_2),
    ._5(n32bit_decoder_short_2__5));
  _7_Segment_Display u_7_segment_display_3 (.g(n32bit_decoder_short_3_sign));  // open: f, a, b, e, d, c, dp
  _32bit_decoder_short u_32bit_decoder_short_3 (
    .sign(n32bit_decoder_short_3_sign), ._4(n32bit_decoder_short_3__4), ._3(n32bit_decoder_short_3__3),
    ._2_2(n32bit_decoder_short_3__2_2), ._1_2(n32bit_decoder_short_3__1_2), ._0(n32bit_decoder_short_3__0),
    .dot(n32bit_decoder_short_3_dot), .in(_13), ._1(n32bit_decoder_short_3__1),
    ._2(n32bit_decoder_short_3__2), ._3_2(n32bit_decoder_short_3__3_2), ._4_2(n32bit_decoder_short_3__4_2),
    ._5(n32bit_decoder_short_3__5));
  matrix_reg_rev matrix_reg_rev_1 (
    .in_1(clk), .in_12(R2_12), .in_22(R2_22), .in_32(R2_32), .in_13(R2_13), .in_23(R2_23), .in_33(R2_33),
    .out_11(matrix_reg_rev_1_out_11), .out_21(matrix_reg_rev_1_out_21), .out_31(matrix_reg_rev_1_out_31),
    .out_12(matrix_reg_rev_1_out_12), .out_22(matrix_reg_rev_1_out_22), .out_32(matrix_reg_rev_1_out_32),
    .out_13(matrix_reg_rev_1_out_13), .out_23(matrix_reg_rev_1_out_23), .out_33(matrix_reg_rev_1_out_33),
    .in_11(R2_11), .in_21(R2_21), .in_31(R2_31));
  matrix_reg_rev matrix_reg_rev_2 (
    .in_1(clk), .in_12(R1_12), .in_22(R1_22), .in_32(R1_32), .in_13(R1_13), .in_23(R1_23), .in_33(R1_33),
    .out_11(matrix_reg_rev_2_out_11), .out_21(matrix_reg_rev_2_out_21), .out_31(matrix_reg_rev_2_out_31),
    .out_12(matrix_reg_rev_2_out_12), .out_22(matrix_reg_rev_2_out_22), .out_32(matrix_reg_rev_2_out_32),
    .out_13(matrix_reg_rev_2_out_13), .out_23(matrix_reg_rev_2_out_23), .out_33(matrix_reg_rev_2_out_33),
    .in_11(R1_11), .in_21(R1_21), .in_31(R1_31));
  Hex_Digit_Display hex_digit_display_1 (.value(n32bit_decoder_short_1__4));  // open: dp
  Hex_Digit_Display hex_digit_display_2 (.value(n32bit_decoder_short_1__3));  // open: dp
  Hex_Digit_Display hex_digit_display_3 (.value(n32bit_decoder_short_2__4));  // open: dp
  Hex_Digit_Display hex_digit_display_4 (.value(n32bit_decoder_short_2__3));  // open: dp
  Hex_Digit_Display hex_digit_display_5 (.value(n32bit_decoder_short_3__3));  // open: dp
  Hex_Digit_Display hex_digit_display_6 (.value(n32bit_decoder_short_3__4));  // open: dp
  matrix_mult matrix_mult_1 (
    .in_1(matrix_reg_rev_1_out_11), .in_2(matrix_reg_rev_1_out_21), .in_3(matrix_reg_rev_1_out_31),
    .in_4(matrix_reg_rev_1_out_12), .in_5(matrix_reg_rev_1_out_22), .in_6(matrix_reg_rev_1_out_32),
    .in_7(matrix_reg_rev_1_out_13), .in_8(matrix_reg_rev_1_out_23), .in_9(matrix_reg_rev_1_out_33),
    .in_10(matrix_reg_rev_2_out_11), .in_11(matrix_reg_rev_2_out_21), .in_12(matrix_reg_rev_2_out_31),
    .in_13(matrix_reg_rev_2_out_12), .in_14(matrix_reg_rev_2_out_22), .in_15(matrix_reg_rev_2_out_32),
    .in_16(matrix_reg_rev_2_out_13), .in_17(matrix_reg_rev_2_out_23), .in_18(matrix_reg_rev_2_out_33),
    .out11(_11), .out21(_21), .out31(_31), .out12(_12), .out22(_22), .out32(_32), .out13(_13), .out23(_23),
    .out33(_33));
  Hex_Digit_Display hex_digit_display_7 (.value(n32bit_decoder_short_1__2_2));  // open: dp
  Hex_Digit_Display hex_digit_display_8 (.value(n32bit_decoder_short_1__1_2));  // open: dp
  Hex_Digit_Display hex_digit_display_9 (.value(n32bit_decoder_short_2__2_2));  // open: dp
  Hex_Digit_Display hex_digit_display_10 (.value(n32bit_decoder_short_2__1_2));  // open: dp
  Hex_Digit_Display hex_digit_display_11 (.value(n32bit_decoder_short_3__1_2));  // open: dp
  Hex_Digit_Display hex_digit_display_12 (.value(n32bit_decoder_short_3__2_2));  // open: dp
  Hex_Digit_Display hex_digit_display_13 (.value(n32bit_decoder_short_1__1));  // open: dp
  Hex_Digit_Display hex_digit_display_14 (.value(n32bit_decoder_short_1__0), .dp(n32bit_decoder_short_1_dot));
  Hex_Digit_Display hex_digit_display_15 (.value(n32bit_decoder_short_2__0), .dp(n32bit_decoder_short_2_dot));
  Hex_Digit_Display hex_digit_display_16 (.value(n32bit_decoder_short_2__1));  // open: dp
  Hex_Digit_Display hex_digit_display_17 (.value(n32bit_decoder_short_3__1));  // open: dp
  Hex_Digit_Display hex_digit_display_18 (.value(n32bit_decoder_short_3__0), .dp(n32bit_decoder_short_3_dot));
  Hex_Digit_Display hex_digit_display_19 (.value(n32bit_decoder_short_1__3_2));  // open: dp
  Hex_Digit_Display hex_digit_display_20 (.value(n32bit_decoder_short_1__2));  // open: dp
  Hex_Digit_Display hex_digit_display_21 (.value(n32bit_decoder_short_2__3_2));  // open: dp
  Hex_Digit_Display hex_digit_display_22 (.value(n32bit_decoder_short_2__2));  // open: dp
  Hex_Digit_Display hex_digit_display_23 (.value(n32bit_decoder_short_3__3_2));  // open: dp
  Hex_Digit_Display hex_digit_display_24 (.value(n32bit_decoder_short_3__2));  // open: dp
  Hex_Digit_Display hex_digit_display_25 (.value(n32bit_decoder_short_1__5));  // open: dp
  Hex_Digit_Display hex_digit_display_26 (.value(n32bit_decoder_short_1__4_2));  // open: dp
  Hex_Digit_Display hex_digit_display_27 (.value(n32bit_decoder_short_2__4_2));  // open: dp
  Hex_Digit_Display hex_digit_display_28 (.value(n32bit_decoder_short_2__5));  // open: dp
  Hex_Digit_Display hex_digit_display_29 (.value(n32bit_decoder_short_3__4_2));  // open: dp
  Hex_Digit_Display hex_digit_display_30 (.value(n32bit_decoder_short_3__5));  // open: dp
  _7_Segment_Display u_7_segment_display_4 (.g(n32bit_decoder_short_4_sign));  // open: f, a, b, e, d, c, dp
  _32bit_decoder_short u_32bit_decoder_short_4 (
    .sign(n32bit_decoder_short_4_sign), ._4(n32bit_decoder_short_4__4), ._3(n32bit_decoder_short_4__3),
    ._2_2(n32bit_decoder_short_4__2_2), ._1_2(n32bit_decoder_short_4__1_2), ._0(n32bit_decoder_short_4__0),
    .dot(n32bit_decoder_short_4_dot), .in(_21), ._1(n32bit_decoder_short_4__1),
    ._2(n32bit_decoder_short_4__2), ._3_2(n32bit_decoder_short_4__3_2), ._4_2(n32bit_decoder_short_4__4_2),
    ._5(n32bit_decoder_short_4__5));
  _7_Segment_Display u_7_segment_display_5 (.g(n32bit_decoder_short_5_sign));  // open: f, a, b, e, d, c, dp
  _32bit_decoder_short u_32bit_decoder_short_5 (
    .sign(n32bit_decoder_short_5_sign), ._4(n32bit_decoder_short_5__4), ._3(n32bit_decoder_short_5__3),
    ._2_2(n32bit_decoder_short_5__2_2), ._1_2(n32bit_decoder_short_5__1_2), ._0(n32bit_decoder_short_5__0),
    .dot(n32bit_decoder_short_5_dot), .in(_22), ._1(n32bit_decoder_short_5__1),
    ._2(n32bit_decoder_short_5__2), ._3_2(n32bit_decoder_short_5__3_2), ._4_2(n32bit_decoder_short_5__4_2),
    ._5(n32bit_decoder_short_5__5));
  _7_Segment_Display u_7_segment_display_6 (.g(n32bit_decoder_short_6_sign));  // open: f, a, b, e, d, c, dp
  _32bit_decoder_short u_32bit_decoder_short_6 (
    .sign(n32bit_decoder_short_6_sign), ._4(n32bit_decoder_short_6__4), ._3(n32bit_decoder_short_6__3),
    ._2_2(n32bit_decoder_short_6__2_2), ._1_2(n32bit_decoder_short_6__1_2), ._0(n32bit_decoder_short_6__0),
    .dot(n32bit_decoder_short_6_dot), .in(_23), ._1(n32bit_decoder_short_6__1),
    ._2(n32bit_decoder_short_6__2), ._3_2(n32bit_decoder_short_6__3_2), ._4_2(n32bit_decoder_short_6__4_2),
    ._5(n32bit_decoder_short_6__5));
  Hex_Digit_Display hex_digit_display_31 (.value(n32bit_decoder_short_4__4));  // open: dp
  Hex_Digit_Display hex_digit_display_32 (.value(n32bit_decoder_short_5__4));  // open: dp
  Hex_Digit_Display hex_digit_display_33 (.value(n32bit_decoder_short_6__4));  // open: dp
  Hex_Digit_Display hex_digit_display_34 (.value(n32bit_decoder_short_4__3));  // open: dp
  Hex_Digit_Display hex_digit_display_35 (.value(n32bit_decoder_short_4__2_2));  // open: dp
  Hex_Digit_Display hex_digit_display_36 (.value(n32bit_decoder_short_5__2_2));  // open: dp
  Hex_Digit_Display hex_digit_display_37 (.value(n32bit_decoder_short_5__3));  // open: dp
  Hex_Digit_Display hex_digit_display_38 (.value(n32bit_decoder_short_6__2_2));  // open: dp
  Hex_Digit_Display hex_digit_display_39 (.value(n32bit_decoder_short_6__3));  // open: dp
  Hex_Digit_Display hex_digit_display_40 (.value(n32bit_decoder_short_4__1_2));  // open: dp
  Hex_Digit_Display hex_digit_display_41 (.value(n32bit_decoder_short_4__0), .dp(n32bit_decoder_short_4_dot));
  Hex_Digit_Display hex_digit_display_42 (.value(n32bit_decoder_short_5__1_2));  // open: dp
  Hex_Digit_Display hex_digit_display_43 (.value(n32bit_decoder_short_5__0), .dp(n32bit_decoder_short_5_dot));
  Hex_Digit_Display hex_digit_display_44 (.value(n32bit_decoder_short_6__0), .dp(n32bit_decoder_short_6_dot));
  Hex_Digit_Display hex_digit_display_45 (.value(n32bit_decoder_short_6__1_2));  // open: dp
  Hex_Digit_Display hex_digit_display_46 (.value(n32bit_decoder_short_4__1));  // open: dp
  Hex_Digit_Display hex_digit_display_47 (.value(n32bit_decoder_short_4__2));  // open: dp
  Hex_Digit_Display hex_digit_display_48 (.value(n32bit_decoder_short_5__1));  // open: dp
  Hex_Digit_Display hex_digit_display_49 (.value(n32bit_decoder_short_5__2));  // open: dp
  Hex_Digit_Display hex_digit_display_50 (.value(n32bit_decoder_short_6__1));  // open: dp
  Hex_Digit_Display hex_digit_display_51 (.value(n32bit_decoder_short_6__2));  // open: dp
  Hex_Digit_Display hex_digit_display_52 (.value(n32bit_decoder_short_4__3_2));  // open: dp
  Hex_Digit_Display hex_digit_display_53 (.value(n32bit_decoder_short_4__4_2));  // open: dp
  Hex_Digit_Display hex_digit_display_54 (.value(n32bit_decoder_short_5__4_2));  // open: dp
  Hex_Digit_Display hex_digit_display_55 (.value(n32bit_decoder_short_5__3_2));  // open: dp
  Hex_Digit_Display hex_digit_display_56 (.value(n32bit_decoder_short_6__4_2));  // open: dp
  Hex_Digit_Display hex_digit_display_57 (.value(n32bit_decoder_short_6__3_2));  // open: dp
  Hex_Digit_Display hex_digit_display_58 (.value(n32bit_decoder_short_4__5));  // open: dp
  Hex_Digit_Display hex_digit_display_59 (.value(n32bit_decoder_short_5__5));  // open: dp
  Hex_Digit_Display hex_digit_display_60 (.value(n32bit_decoder_short_6__5));  // open: dp
  _7_Segment_Display u_7_segment_display_7 (.g(n32bit_decoder_short_7_sign));  // open: f, a, b, e, d, c, dp
  _32bit_decoder_short u_32bit_decoder_short_7 (
    .sign(n32bit_decoder_short_7_sign), ._4(n32bit_decoder_short_7__4), ._3(n32bit_decoder_short_7__3),
    ._2_2(n32bit_decoder_short_7__2_2), ._1_2(n32bit_decoder_short_7__1_2), ._0(n32bit_decoder_short_7__0),
    .dot(n32bit_decoder_short_7_dot), .in(_31), ._1(n32bit_decoder_short_7__1),
    ._2(n32bit_decoder_short_7__2), ._3_2(n32bit_decoder_short_7__3_2), ._4_2(n32bit_decoder_short_7__4_2),
    ._5(n32bit_decoder_short_7__5));
  _7_Segment_Display u_7_segment_display_8 (.g(n32bit_decoder_short_8_sign));  // open: f, a, b, e, d, c, dp
  _32bit_decoder_short u_32bit_decoder_short_8 (
    .sign(n32bit_decoder_short_8_sign), ._4(n32bit_decoder_short_8__4), ._3(n32bit_decoder_short_8__3),
    ._2_2(n32bit_decoder_short_8__2_2), ._1_2(n32bit_decoder_short_8__1_2), ._0(n32bit_decoder_short_8__0),
    .dot(n32bit_decoder_short_8_dot), .in(_32), ._1(n32bit_decoder_short_8__1),
    ._2(n32bit_decoder_short_8__2), ._3_2(n32bit_decoder_short_8__3_2), ._4_2(n32bit_decoder_short_8__4_2),
    ._5(n32bit_decoder_short_8__5));
  _7_Segment_Display u_7_segment_display_9 (.g(n32bit_decoder_short_9_sign));  // open: f, a, b, e, d, c, dp
  _32bit_decoder_short u_32bit_decoder_short_9 (
    .sign(n32bit_decoder_short_9_sign), ._4(n32bit_decoder_short_9__4), ._3(n32bit_decoder_short_9__3),
    ._2_2(n32bit_decoder_short_9__2_2), ._1_2(n32bit_decoder_short_9__1_2), ._0(n32bit_decoder_short_9__0),
    .dot(n32bit_decoder_short_9_dot), .in(_33), ._1(n32bit_decoder_short_9__1),
    ._2(n32bit_decoder_short_9__2), ._3_2(n32bit_decoder_short_9__3_2), ._4_2(n32bit_decoder_short_9__4_2),
    ._5(n32bit_decoder_short_9__5));
  Hex_Digit_Display hex_digit_display_61 (.value(n32bit_decoder_short_7__4));  // open: dp
  Hex_Digit_Display hex_digit_display_62 (.value(n32bit_decoder_short_7__3));  // open: dp
  Hex_Digit_Display hex_digit_display_63 (.value(n32bit_decoder_short_8__4));  // open: dp
  Hex_Digit_Display hex_digit_display_64 (.value(n32bit_decoder_short_8__3));  // open: dp
  Hex_Digit_Display hex_digit_display_65 (.value(n32bit_decoder_short_9__4));  // open: dp
  Hex_Digit_Display hex_digit_display_66 (.value(n32bit_decoder_short_9__3));  // open: dp
  Hex_Digit_Display hex_digit_display_67 (.value(n32bit_decoder_short_7__2_2));  // open: dp
  Hex_Digit_Display hex_digit_display_68 (.value(n32bit_decoder_short_7__1_2));  // open: dp
  Hex_Digit_Display hex_digit_display_69 (.value(n32bit_decoder_short_8__2_2));  // open: dp
  Hex_Digit_Display hex_digit_display_70 (.value(n32bit_decoder_short_8__1_2));  // open: dp
  Hex_Digit_Display hex_digit_display_71 (.value(n32bit_decoder_short_9__1_2));  // open: dp
  Hex_Digit_Display hex_digit_display_72 (.value(n32bit_decoder_short_9__2_2));  // open: dp
  Button update (.out(update_out));
  Button reset (.out(reset_out));
  Hex_Digit_Display hex_digit_display_73 (.value(n32bit_decoder_short_7__1));  // open: dp
  Hex_Digit_Display hex_digit_display_74 (.value(n32bit_decoder_short_7__0), .dp(n32bit_decoder_short_7_dot));
  Hex_Digit_Display hex_digit_display_75 (.value(n32bit_decoder_short_8__0), .dp(n32bit_decoder_short_8_dot));
  Hex_Digit_Display hex_digit_display_76 (.value(n32bit_decoder_short_8__1));  // open: dp
  Hex_Digit_Display hex_digit_display_77 (.value(n32bit_decoder_short_9__0), .dp(n32bit_decoder_short_9_dot));
  Hex_Digit_Display hex_digit_display_78 (.value(n32bit_decoder_short_9__1));  // open: dp
  Hex_Digit_Display hex_digit_display_79 (.value(n32bit_decoder_short_7__3_2));  // open: dp
  Hex_Digit_Display hex_digit_display_80 (.value(n32bit_decoder_short_7__2));  // open: dp
  Hex_Digit_Display hex_digit_display_81 (.value(n32bit_decoder_short_8__2));  // open: dp
  Hex_Digit_Display hex_digit_display_82 (.value(n32bit_decoder_short_8__3_2));  // open: dp
  Hex_Digit_Display hex_digit_display_83 (.value(n32bit_decoder_short_9__2));  // open: dp
  Hex_Digit_Display hex_digit_display_84 (.value(n32bit_decoder_short_9__3_2));  // open: dp
  // DotMatrix #(.inputtype("select"), .matrixcols(32), .matrixrows(32), .persist(128)) dotmatrix_1: pin names not known; wires that end beside it: dotmatrix_1_p1, dotmatrix_1_p2
  _64x64_display_controller u_64x64_display_controller_1 (
    .clk(clk), .x11(dotmatrix_1_p1), .x21(n64x64_display_controller_1_x21),
    .x12(n64x64_display_controller_1_x12), .x22(n64x64_display_controller_1_x22), .y11(dotmatrix_1_p2),
    .y21(n64x64_display_controller_1_y21), .y12(n64x64_display_controller_1_y12),
    .y22(n64x64_display_controller_1_y22), .x(x), .y(y), .clear(reset_out), .state(state),
    .update_frame(update_out));
  // DotMatrix #(.inputtype("select"), .matrixcols(32), .matrixrows(32), .persist(128)) dotmatrix_2: pin names not known; wires that end beside it: n64x64_display_controller_1_x12, n64x64_display_controller_1_y12
  Hex_Digit_Display hex_digit_display_85 (.value(n32bit_decoder_short_7__5));  // open: dp
  Hex_Digit_Display hex_digit_display_86 (.value(n32bit_decoder_short_7__4_2));  // open: dp
  Hex_Digit_Display hex_digit_display_87 (.value(n32bit_decoder_short_8__4_2));  // open: dp
  Hex_Digit_Display hex_digit_display_88 (.value(n32bit_decoder_short_8__5));  // open: dp
  Hex_Digit_Display hex_digit_display_89 (.value(n32bit_decoder_short_9__4_2));  // open: dp
  Hex_Digit_Display hex_digit_display_90 (.value(n32bit_decoder_short_9__5));  // open: dp
  // DotMatrix #(.inputtype("select"), .matrixcols(32), .matrixrows(32), .persist(128)) dotmatrix_3: pin names not known; wires that end beside it: n64x64_display_controller_1_x21, n64x64_display_controller_1_y21
  // DotMatrix #(.inputtype("select"), .matrixcols(32), .matrixrows(32), .persist(128)) dotmatrix_4: pin names not known; wires that end beside it: n64x64_display_controller_1_x22, n64x64_display_controller_1_y22

  // Other names for the same wires on the sheet: A11[31:0] = in_1; A12[31:0] = in_4; A13[31:0] = in_7;
  //   A21[31:0] = in_2; A22[31:0] = in_5; A23[31:0] = in_8; A31[31:0] = in_3; A32[31:0] = in_6; A33[31:0] = in_9

  // Notes on the sheet:
  //   in_1: pull=down
  //   in_4: pull=down
  //   in_9: pull=down
  //   in_8: pull=down
  //   in_5: pull=down
  //   in_3: pull=down
  //   in_2: pull=down
  //   Load_sample: pull=down
  //   in_6: pull=down
  //   in_7: pull=down
endmodule

module matrix_mult_sub (
  input  [31:0] in_a1,
  input  [31:0] in_b1,
  input  [31:0] in_a2,
  input  [31:0] in_b2,
  input  [31:0] in_a3,
  input  [31:0] in_b3,
  output [31:0] out_ab
);

  wire [31:0] adder_1_out, fp_mult_1_out, fp_mult_2_out, fp_mult_3_out;

  fp_mult fp_mult_1 (.in1(in_a1), .in2(in_b1), .out(fp_mult_1_out));
  fp_mult fp_mult_2 (.in1(in_a2), .in2(in_b2), .out(fp_mult_2_out));
  fp_mult fp_mult_3 (.in1(in_a3), .in2(in_b3), .out(fp_mult_3_out));
  Adder #(.width(32)) adder_1 (.a(fp_mult_1_out), .b(fp_mult_2_out), .out(adder_1_out));  // open: cin, cout
  Adder #(.width(32)) adder_2 (.a(adder_1_out), .b(fp_mult_3_out), .out(out_ab));  // open: cin, cout

  // Notes on the sheet:
  //   in_a3: pull=down
  //   in_a1: pull=down
  //   in_b3: pull=down
  //   in_a2: pull=down
  //   in_b2: pull=down
  //   in_b1: pull=down
  //   out_ab: pull=down
endmodule

module matrix_mult (
  input  [31:0] in_1,
  input  [31:0] in_2,
  input  [31:0] in_3,
  input  [31:0] in_4,
  input  [31:0] in_5,
  input  [31:0] in_6,
  input  [31:0] in_7,
  input  [31:0] in_8,
  input  [31:0] in_9,
  input  [31:0] in_10,
  input  [31:0] in_11,
  input  [31:0] in_12,
  input  [31:0] in_13,
  input  [31:0] in_14,
  input  [31:0] in_15,
  input  [31:0] in_16,
  input  [31:0] in_17,
  input  [31:0] in_18,
  output [31:0] out11,
  output [31:0] out21,
  output [31:0] out31,
  output [31:0] out12,
  output [31:0] out22,
  output [31:0] out32,
  output [31:0] out13,
  output [31:0] out23,
  output [31:0] out33
);

  matrix_mult_sub matrix_mult_sub_1 (
    .in_a1(in_10), .in_b1(in_1), .in_a2(in_11), .in_b2(in_4), .in_a3(in_12), .in_b3(in_7), .out_ab(out11));
  matrix_mult_sub matrix_mult_sub_2 (
    .in_a1(in_13), .in_b1(in_1), .in_a2(in_14), .in_b2(in_4), .in_a3(in_15), .in_b3(in_7), .out_ab(out12));
  matrix_mult_sub matrix_mult_sub_3 (
    .in_a1(in_16), .in_b1(in_1), .in_a2(in_17), .in_b2(in_4), .in_a3(in_18), .in_b3(in_7), .out_ab(out13));
  matrix_mult_sub matrix_mult_sub_4 (
    .in_a1(in_10), .in_b1(in_2), .in_a2(in_11), .in_b2(in_5), .in_a3(in_12), .in_b3(in_8), .out_ab(out21));
  matrix_mult_sub matrix_mult_sub_5 (
    .in_a1(in_13), .in_b1(in_2), .in_a2(in_14), .in_b2(in_5), .in_a3(in_15), .in_b3(in_8), .out_ab(out22));
  matrix_mult_sub matrix_mult_sub_6 (
    .in_a1(in_16), .in_b1(in_2), .in_a2(in_17), .in_b2(in_5), .in_a3(in_18), .in_b3(in_8), .out_ab(out23));
  matrix_mult_sub matrix_mult_sub_7 (
    .in_a1(in_10), .in_b1(in_3), .in_a2(in_11), .in_b2(in_6), .in_a3(in_12), .in_b3(in_9), .out_ab(out31));
  matrix_mult_sub matrix_mult_sub_8 (
    .in_a1(in_13), .in_b1(in_3), .in_a2(in_14), .in_b2(in_6), .in_a3(in_15), .in_b3(in_9), .out_ab(out32));
  matrix_mult_sub matrix_mult_sub_9 (
    .in_a1(in_16), .in_b1(in_3), .in_a2(in_17), .in_b2(in_6), .in_a3(in_18), .in_b3(in_9), .out_ab(out33));

  // Other names for the same wires on the sheet: A11[31:0] = in_10; A12[31:0] = in_13; A13[31:0] = in_16;
  //   A21[31:0] = in_11; A22[31:0] = in_14; A23[31:0] = in_17; A31[31:0] = in_12; A32[31:0] = in_15;
  //   A33[31:0] = in_18; B11[31:0] = in_1; B12[31:0] = in_4; B13[31:0] = in_7; B21[31:0] = in_2; B22[31:0] = in_5;
  //   B23[31:0] = in_8; B31[31:0] = in_3; B32[31:0] = in_6; B33[31:0] = in_9

  // Notes on the sheet:
  //   in_17: pull=down
  //   in_12: pull=down
  //   out13: pull=down
  //   out31: pull=down
  //   in_15: pull=down
  //   in_4: pull=down
  //   in_18: pull=down
  //   in_9: pull=down
  //   out22: pull=down
  //   out32: pull=down
  //   in_10: pull=down
  //   out33: pull=down
  //   in_13: pull=down
  //   out21: pull=down
  //   in_6: pull=down
  //   in_16: pull=down
  //   out23: pull=down
  //   in_8: pull=down
  //   in_11: pull=down
  //   out11: pull=down
  //   in_1: pull=down
  //   in_5: pull=down
  //   in_7: pull=down
  //   in_14: pull=down
  //   in_3: pull=down
  //   in_2: pull=down
  //   out12: pull=down
endmodule

module matrix_reg (
  input  in_1,
  input  [31:0] in_11,
  input  [31:0] in_21,
  input  [31:0] in_31,
  input  [31:0] in_12,
  input  [31:0] in_22,
  input  [31:0] in_32,
  input  [31:0] in_13,
  input  [31:0] in_23,
  input  [31:0] in_33,
  output [31:0] out_11,
  output [31:0] out_21,
  output [31:0] out_31,
  output [31:0] out_12,
  output [31:0] out_22,
  output [31:0] out_32,
  output [31:0] out_13,
  output [31:0] out_23,
  output [31:0] out_33
);

  Register #(.width(32)) register_1 (.D(in_11), .Q(out_11), .clk(in_1));  // open: en, clr
  Register #(.width(32)) register_2 (.D(in_12), .Q(out_12), .clk(in_1));  // open: en, clr
  Register #(.width(32)) register_3 (.D(in_13), .Q(out_13), .clk(in_1));  // open: en, clr
  Register #(.width(32)) register_4 (.D(in_21), .Q(out_21), .clk(in_1));  // open: en, clr
  Register #(.width(32)) register_5 (.D(in_22), .Q(out_22), .clk(in_1));  // open: en, clr
  Register #(.width(32)) register_6 (.D(in_23), .Q(out_23), .clk(in_1));  // open: en, clr
  Register #(.width(32)) register_7 (.D(in_31), .Q(out_31), .clk(in_1));  // open: en, clr
  Register #(.width(32)) register_8 (.D(in_32), .Q(out_32), .clk(in_1));  // open: en, clr
  Register #(.width(32)) register_9 (.D(in_33), .Q(out_33), .clk(in_1));  // open: en, clr

  // Other names for the same wires on the sheet: clk = in_1
endmodule

module matrix_reg_rev (
  input  in_1,
  input  [31:0] in_11,
  input  [31:0] in_21,
  input  [31:0] in_31,
  input  [31:0] in_12,
  input  [31:0] in_22,
  input  [31:0] in_32,
  input  [31:0] in_13,
  input  [31:0] in_23,
  input  [31:0] in_33,
  output [31:0] out_11,
  output [31:0] out_21,
  output [31:0] out_31,
  output [31:0] out_12,
  output [31:0] out_22,
  output [31:0] out_32,
  output [31:0] out_13,
  output [31:0] out_23,
  output [31:0] out_33
);

  Register #(.width(32)) register_1 (.D(in_11), .Q(out_11), .clk(in_1));  // open: en, clr
  Register #(.width(32)) register_2 (.D(in_12), .Q(out_12), .clk(in_1));  // open: en, clr
  Register #(.width(32)) register_3 (.D(in_13), .Q(out_13), .clk(in_1));  // open: en, clr
  Register #(.width(32)) register_4 (.D(in_21), .Q(out_21), .clk(in_1));  // open: en, clr
  Register #(.width(32)) register_5 (.D(in_22), .Q(out_22), .clk(in_1));  // open: en, clr
  Register #(.width(32)) register_6 (.D(in_23), .Q(out_23), .clk(in_1));  // open: en, clr
  Register #(.width(32)) register_7 (.D(in_31), .Q(out_31), .clk(in_1));  // open: en, clr
  Register #(.width(32)) register_8 (.D(in_32), .Q(out_32), .clk(in_1));  // open: en, clr
  Register #(.width(32)) register_9 (.D(in_33), .Q(out_33), .clk(in_1));  // open: en, clr

  // Other names for the same wires on the sheet: clk = in_1
endmodule

module _32bit_decoder (
  input  [31:0] in,
  output sign,
  output [3:0] _4,
  output [3:0] _1,
  output [3:0] _3,
  output [3:0] _2,
  output [3:0] _2_2,
  output [3:0] _3_2,
  output [3:0] _1_2,
  output [3:0] _4_2,
  output [3:0] _0,
  output [3:0] _5,
  output dot,
  output [3:0] _6,
  output [3:0] _7,
  output [3:0] _8,
  output [3:0] _9,
  output [3:0] _10,
  output [3:0] _11,
  output [3:0] _12,
  output [3:0] _13,
  output [3:0] _14,
  output [3:0] _15,
  output [3:0] _16
);

  wire [15:0] n32bit_decoder_10div_1_out, n32bit_decoder_10div_2_out, n32bit_decoder_10div_3_out,
       n32bit_decoder_10div_4_out, n32bit_decoder_10div_5_out, n32bit_decoder_10mul_1_out,
       n32bit_decoder_10mul_2_out, n32bit_decoder_10mul_3_out, n32bit_decoder_10mul_4_out,
       n32bit_decoder_10mul_5_out, n32bit_decoder_10mul_6_out, n32bit_decoder_10mul_7_out,
       n32bit_decoder_10mul_8_out, n32bit_decoder_10mul_9_out, n32bit_decoder_10mul_10_out,
       n32bit_decoder_10mul_11_out, n32bit_decoder_10mul_12_out, n32bit_decoder_10mul_13_out,
       n32bit_decoder_10mul_14_out, n32bit_decoder_10mul_15_out;
  wire [31:0] multiplexer_1_out, subtractor_1_out;

  _32bit_decoder_10div u_32bit_decoder_10div_1 (
    .in(n32bit_decoder_10div_4_out), .out(n32bit_decoder_10div_1_out), .num_out(_3));
  _32bit_decoder_10div u_32bit_decoder_10div_2 (
    .in(n32bit_decoder_10div_1_out), .out(n32bit_decoder_10div_2_out), .num_out(_4));
  Pull_Resistor pull_resistor_1 (.node(sign));
  BitSelector #(.width(32)) bitselector_1 (.in(in), .out(sign), .sel({5{1'b1}}));
  Pull_Resistor pull_resistor_2 (.node(in));
  _32bit_decoder_10div u_32bit_decoder_10div_3 (
    .in(n32bit_decoder_10div_5_out), .out(n32bit_decoder_10div_3_out), .num_out(_1_2));
  _32bit_decoder_10div u_32bit_decoder_10div_4 (
    .in(n32bit_decoder_10div_3_out), .out(n32bit_decoder_10div_4_out), .num_out(_2_2));
  Multiplexer #(.width(32)) multiplexer_1 (
    .in0(in), .in1(subtractor_1_out), .out(multiplexer_1_out), .sel(sign));  // open: en
  Subtractor #(.width(32)) subtractor_1 (.a({32{1'b0}}), .b(in), .out(subtractor_1_out));  // open: bin, bout
  _32bit_decoder_10div u_32bit_decoder_10div_5 (
    .in(multiplexer_1_out[31:16]), .out(n32bit_decoder_10div_5_out), .num_out(_0));
  _32bit_decoder_10mul u_32bit_decoder_10mul_1 (
    .in(multiplexer_1_out[15:0]), .out(n32bit_decoder_10mul_1_out), .num_out(_1));
  _32bit_decoder_10mul u_32bit_decoder_10mul_2 (
    .in(n32bit_decoder_10mul_3_out), .out(n32bit_decoder_10mul_2_out), .num_out(_3_2));
  _32bit_decoder_10mul u_32bit_decoder_10mul_3 (
    .in(n32bit_decoder_10mul_1_out), .out(n32bit_decoder_10mul_3_out), .num_out(_2));
  _32bit_decoder_10mul u_32bit_decoder_10mul_4 (
    .in(n32bit_decoder_10mul_2_out), .out(n32bit_decoder_10mul_4_out), .num_out(_4_2));
  _32bit_decoder_10mul u_32bit_decoder_10mul_5 (
    .in(n32bit_decoder_10mul_4_out), .out(n32bit_decoder_10mul_5_out), .num_out(_5));
  _32bit_decoder_10mul u_32bit_decoder_10mul_6 (
    .in(n32bit_decoder_10mul_5_out), .out(n32bit_decoder_10mul_6_out), .num_out(_6));
  _32bit_decoder_10mul u_32bit_decoder_10mul_7 (
    .in(n32bit_decoder_10mul_6_out), .out(n32bit_decoder_10mul_7_out), .num_out(_7));
  _32bit_decoder_10mul u_32bit_decoder_10mul_8 (
    .in(n32bit_decoder_10mul_9_out), .out(n32bit_decoder_10mul_8_out), .num_out(_9));
  _32bit_decoder_10mul u_32bit_decoder_10mul_9 (
    .in(n32bit_decoder_10mul_7_out), .out(n32bit_decoder_10mul_9_out), .num_out(_8));
  _32bit_decoder_10mul u_32bit_decoder_10mul_10 (
    .in(n32bit_decoder_10mul_11_out), .out(n32bit_decoder_10mul_10_out), .num_out(_11));
  _32bit_decoder_10mul u_32bit_decoder_10mul_11 (
    .in(n32bit_decoder_10mul_8_out), .out(n32bit_decoder_10mul_11_out), .num_out(_10));
  _32bit_decoder_10mul u_32bit_decoder_10mul_12 (
    .in(n32bit_decoder_10mul_10_out), .out(n32bit_decoder_10mul_12_out), .num_out(_12));
  _32bit_decoder_10mul u_32bit_decoder_10mul_13 (
    .in(n32bit_decoder_10mul_12_out), .out(n32bit_decoder_10mul_13_out), .num_out(_13));
  _32bit_decoder_10mul u_32bit_decoder_10mul_14 (
    .in(n32bit_decoder_10mul_13_out), .out(n32bit_decoder_10mul_14_out), .num_out(_14));
  _32bit_decoder_10mul u_32bit_decoder_10mul_15 (
    .in(n32bit_decoder_10mul_14_out), .out(n32bit_decoder_10mul_15_out), .num_out(_15));
  _32bit_decoder_10mul u_32bit_decoder_10mul_16 (.in(n32bit_decoder_10mul_15_out), .num_out(_16));  // open: out

  assign dot = 1'b1;

  // Other names for the same wires on the sheet: tunnel = sign

  // Notes on the sheet:
  //   _0: pull=down
  //   _1_2: pull=down
  //   _16: pull=down
  //   _1: pull=down
  //   _11: pull=down
  //   _6: pull=down
  //   _13: pull=down
  //   _14: pull=down
  //   _4: pull=down
  //   _7: pull=down
  //   _5: pull=down
  //   _2_2: pull=down
  //   _10: pull=down
  //   _3_2: pull=down
  //   in: pull=down
  //   _12: pull=down
  //   _4_2: pull=down
  //   _15: pull=down
  //   _8: pull=down
  //   _2: pull=down
  //   _9: pull=down
  //   _3: pull=down
endmodule

module _32bit_decoder_10div (
  input  [15:0] in,
  output [15:0] out,
  output [3:0] num_out
);

  wire [15:0] divider_1_rem;

  Divider #(.width(16)) divider_1 (.a(in), .b(16'ha), .out(out), .rem(divider_1_rem));  // open: upper
  Bit_Extender #(.in_width(16), .out_width(4)) bit_extender_1 (.in(divider_1_rem), .out(num_out));

  // Notes on the sheet:
  //   in: pull=down
  //   num_out: pull=down
  //   out: pull=down
endmodule

module _32bit_decoder_10mul (
  input  [15:0] in,
  output [15:0] out,
  output [3:0] num_out
);

  wire [15:4] multiplier_1_cout;

  Multiplier #(.width(16)) multiplier_1 (
    .a(in), .b(16'ha), .out(out), .cout({multiplier_1_cout, num_out}));  // open: cin
  Pull_Resistor pull_resistor_1 (.node(num_out));
endmodule

module _32bit_decoder_short (
  input  [31:0] in,
  output sign,
  output [3:0] _4,
  output [3:0] _1,
  output [3:0] _3,
  output [3:0] _2,
  output [3:0] _2_2,
  output [3:0] _3_2,
  output [3:0] _1_2,
  output [3:0] _4_2,
  output [3:0] _0,
  output [3:0] _5,
  output dot
);

  wire [15:0] n32bit_decoder_10div_2_out, n32bit_decoder_10div_3_out, n32bit_decoder_10div_4_out,
       n32bit_decoder_10div_5_out, n32bit_decoder_10mul_1_out, n32bit_decoder_10mul_2_out,
       n32bit_decoder_10mul_3_out, n32bit_decoder_10mul_4_out;
  wire [31:0] multiplexer_1_out, subtractor_1_out;

  _32bit_decoder_10div u_32bit_decoder_10div_1 (.in(n32bit_decoder_10div_2_out), .num_out(_4));  // open: out
  _32bit_decoder_10div u_32bit_decoder_10div_2 (
    .in(n32bit_decoder_10div_3_out), .out(n32bit_decoder_10div_2_out), .num_out(_3));
  Pull_Resistor pull_resistor_1 (.node(sign));
  BitSelector #(.width(32)) bitselector_1 (.in(in), .out(sign), .sel({5{1'b1}}));
  Pull_Resistor pull_resistor_2 (.node(in));
  _32bit_decoder_10div u_32bit_decoder_10div_3 (
    .in(n32bit_decoder_10div_4_out), .out(n32bit_decoder_10div_3_out), .num_out(_2_2));
  _32bit_decoder_10div u_32bit_decoder_10div_4 (
    .in(n32bit_decoder_10div_5_out), .out(n32bit_decoder_10div_4_out), .num_out(_1_2));
  Multiplexer #(.width(32)) multiplexer_1 (
    .in0(in), .in1(subtractor_1_out), .out(multiplexer_1_out), .sel(sign));  // open: en
  Subtractor #(.width(32)) subtractor_1 (.a({32{1'b0}}), .b(in), .out(subtractor_1_out));  // open: bin, bout
  _32bit_decoder_10mul u_32bit_decoder_10mul_1 (
    .in(multiplexer_1_out[15:0]), .out(n32bit_decoder_10mul_1_out), .num_out(_1));
  _32bit_decoder_10div u_32bit_decoder_10div_5 (
    .in(multiplexer_1_out[31:16]), .out(n32bit_decoder_10div_5_out), .num_out(_0));
  _32bit_decoder_10mul u_32bit_decoder_10mul_2 (
    .in(n32bit_decoder_10mul_1_out), .out(n32bit_decoder_10mul_2_out), .num_out(_2));
  _32bit_decoder_10mul u_32bit_decoder_10mul_3 (
    .in(n32bit_decoder_10mul_2_out), .out(n32bit_decoder_10mul_3_out), .num_out(_3_2));
  _32bit_decoder_10mul u_32bit_decoder_10mul_4 (
    .in(n32bit_decoder_10mul_3_out), .out(n32bit_decoder_10mul_4_out), .num_out(_4_2));
  _32bit_decoder_10mul u_32bit_decoder_10mul_5 (.in(n32bit_decoder_10mul_4_out), .num_out(_5));  // open: out

  assign dot = 1'b1;

  // Other names for the same wires on the sheet: tunnel = sign

  // Notes on the sheet:
  //   _4_2: pull=down
  //   _1_2: pull=down
  //   _4: pull=down
  //   _2: pull=down
  //   _3: pull=down
  //   _0: pull=down
  //   _3_2: pull=down
  //   _5: pull=down
  //   _1: pull=down
  //   in: pull=down
  //   _2_2: pull=down
endmodule

module matrix_input (
  input  [31:0] in_1,
  input  [31:0] in_2,
  input  [31:0] in_3,
  input  [31:0] in_4,
  input  [31:0] in_5,
  input  [31:0] in_6,
  input  [31:0] in_7,
  input  [31:0] in_8,
  input  [31:0] in_9,
  output [31:0] out11,
  output [31:0] out21,
  output [31:0] out31,
  output [31:0] out12,
  output [31:0] out22,
  output [31:0] out32,
  output [31:0] out13,
  output [31:0] out23,
  output [31:0] out33
);


  assign out11 = in_1;
  assign out12 = in_4;
  assign out13 = in_7;
  assign out21 = in_2;
  assign out22 = in_5;
  assign out23 = in_8;
  assign out31 = in_3;
  assign out32 = in_6;
  assign out33 = in_9;

  // Other names for the same wires on the sheet: _11[31:0] = in_1; _12[31:0] = in_4; _13[31:0] = in_7;
  //   _21[31:0] = in_2; _22[31:0] = in_5; _23[31:0] = in_8; _31[31:0] = in_3; _32[31:0] = in_6; _33[31:0] = in_9
endmodule

module fp_mult (
  input  [31:0] in1,
  input  [31:0] in2,
  output [31:0] out
);

  wire [31:0] multiplier_1_cout, multiplier_1_out, shifter_1_out, shifter_2_out, undriven;

  Multiplier #(.width(32)) multiplier_1 (
    .a(in1), .b(in2), .out(multiplier_1_out), .cin(undriven), .cout(multiplier_1_cout));
  Shifter #(.width(32), .shift("lr")) shifter_1 (.in(multiplier_1_out), .\dist (5'b10000), .out(shifter_1_out));
  Shifter #(.width(32)) shifter_2 (.in(multiplier_1_cout), .\dist (5'b10000), .out(shifter_2_out));
  Adder #(.width(32)) adder_1 (.a(shifter_1_out), .b(shifter_2_out), .out(out));  // open: cin, cout

  // Notes on the sheet:
  //   in1: pull=down
  //   in2: pull=down
  //   out: pull=down
  //   for now ignore
  //   TODO?: take care of carry (in both case the carry is out of 32bit bounds
endmodule

module fp_div (
  input  [31:0] in1,
  input  [31:0] in2,
  output [31:0] out
);

  wire [31:0] divider_1_out, divider_1_rem, divider_2_out, shifter_1_out, shifter_2_out;

  Divider #(.width(32)) divider_1 (.a(in1), .b(in2), .out(divider_1_out), .rem(divider_1_rem));  // open: upper
  Shifter #(.width(32), .shift("lr")) shifter_1 (.in(in2), .\dist (5'b10000), .out(shifter_1_out));
  Shifter #(.width(32)) shifter_2 (.in(divider_1_out), .\dist (5'b10000), .out(shifter_2_out));
  Divider #(.width(32)) divider_2 (.a(divider_1_rem), .b(shifter_1_out), .out(divider_2_out));  // open: upper, rem
  Adder #(.width(32)) adder_1 (.a(shifter_2_out), .b(divider_2_out), .out(out));  // open: cin, cout

  // Notes on the sheet:
  //   out: pull=down
  //   in2: pull=down
  //   in1: pull=down
endmodule

module fp_to_int (
  input  [31:0] in,
  output [31:0] out
);

  Shifter #(.width(32), .shift("lr")) shifter_1 (.in(in), .\dist (5'b10000), .out(out));

  // Notes on the sheet:
  //   out: pull=down
  //   in: pull=down
endmodule

module _64x64_display_controller (
  input  [5:0] y,
  input  [5:0] x,
  input  state,
  input  clear,
  input  update_frame,
  input  clk,
  output [31:0] x12,
  output [31:0] x22,
  output [31:0] x11,
  output [31:0] x21,
  output [31:0] y12,
  output [31:0] y22,
  output [31:0] y11,
  output [31:0] y21
);

  wire and_1_out, and_2_out, and_3_out, counter_1_carry, counter_2_carry, multiplexer_1_out,
       multiplexer_2_out, multiplexer_3_out, multiplexer_6_out, not_1_out, not_2_out, not_3_out, not_4_out,
       not_5_out, not_6_out, or_1_out, s_r_ff_1_qn, s_r_ff_2_q, s_r_ff_3_q;
  wire [5:0] counter_2_q, multiplexer_5_out, register_1_q, register_2_q;
  wire [31:0] decoder_1_out0, decoder_2_out0, multiplexer_7_out, multiplexer_8_out, or_2_out,
       pull_resistor_2_node, ram_1_data, ram_2_data, ram_3_data, ram_4_data;

  not not_1 (not_1_out, update_frame);
  and and_1 (and_1_out, update_frame, s_r_ff_1_qn);
  S_R_Flip_Flop s_r_ff_1 (.Qn(s_r_ff_1_qn), .preset(s_r_ff_2_q), .reset(not_1_out));  // open: S, clk, R, Q, en
  Register #(.width(6)) register_1 (.D(y), .Q(register_1_q), .clk(clk));  // open: en, clr
  Register #(.width(6)) register_2 (.D(x), .Q(register_2_q), .clk(clk));  // open: en, clr
  S_R_Flip_Flop s_r_ff_2 (.Q(s_r_ff_2_q), .preset(and_1_out), .reset(counter_1_carry));  // open: S, clk, R, Qn, en
  Decoder #(.select(5)) decoder_1 (
    .out0(decoder_1_out0[0]), .out1(decoder_1_out0[1]), .out2(decoder_1_out0[2]), .out3(decoder_1_out0[3]),
    .out4(decoder_1_out0[4]), .out5(decoder_1_out0[5]), .out6(decoder_1_out0[6]), .out7(decoder_1_out0[7]),
    .out8(decoder_1_out0[8]), .out9(decoder_1_out0[9]), .out10(decoder_1_out0[10]),
    .out11(decoder_1_out0[11]), .out12(decoder_1_out0[12]), .out13(decoder_1_out0[13]),
    .out14(decoder_1_out0[14]), .out15(decoder_1_out0[15]), .out16(decoder_1_out0[16]),
    .out17(decoder_1_out0[17]), .out18(decoder_1_out0[18]), .out19(decoder_1_out0[19]),
    .out20(decoder_1_out0[20]), .out21(decoder_1_out0[21]), .out22(decoder_1_out0[22]),
    .out23(decoder_1_out0[23]), .out24(decoder_1_out0[24]), .out25(decoder_1_out0[25]),
    .out26(decoder_1_out0[26]), .out27(decoder_1_out0[27]), .out28(decoder_1_out0[28]),
    .out29(decoder_1_out0[29]), .out30(decoder_1_out0[30]), .out31(decoder_1_out0[31]),
    .sel(register_2_q[4:0]), .en(state));
  and and_2 (and_2_out, s_r_ff_2_q, counter_2_carry);
  Pull_Resistor pull_resistor_1 (.node(decoder_1_out0));
  S_R_Flip_Flop s_r_ff_3 (
    .S(and_2_out), .clk(clk), .R(counter_1_carry), .Q(s_r_ff_3_q));  // open: Qn, preset, reset, en
  Multiplexer multiplexer_1 (.in0(state), .in1(1'b0), .out(multiplexer_1_out), .sel(s_r_ff_3_q));  // open: en
  Counter #(.width(6), .max('h3f)) counter_1 (
    .carry(counter_1_carry), .clk(and_3_out));  // open: load, D, count, Q, clr
  and and_3 (and_3_out, clk, s_r_ff_3_q);
  Pull_Resistor pull_resistor_2 (.node(pull_resistor_2_node));
  not not_2 (not_2_out, register_2_q[5]);
  or or_1 (or_1_out, clear, clear);
  assign or_2_out = pull_resistor_2_node | decoder_1_out0;  // OR_Gate or_2, 32 bits wide
  Multiplexer multiplexer_2 (.in0(register_2_q[5]), .in1(1'b1), .out(multiplexer_2_out), .sel(s_r_ff_3_q));  // open: en
  Multiplexer multiplexer_3 (.in0(not_2_out), .in1(1'b1), .out(multiplexer_3_out), .sel(s_r_ff_3_q));  // open: en
  Multiplexer #(.width(32)) multiplexer_4 (
    .in0(ram_3_data), .in1(ram_1_data), .out(pull_resistor_2_node), .sel(multiplexer_3_out), .en(not_3_out));
  Multiplexer #(.width(6)) multiplexer_5 (
    .in0(register_1_q), .in1(counter_2_q), .out(multiplexer_5_out), .sel(s_r_ff_3_q));  // open: en
  Counter #(.width(6), .max('h3f)) counter_2 (
    .Q(counter_2_q), .carry(counter_2_carry), .clk(clk));  // open: load, D, count, clr
  ROM #(.addrWidth(6), .dataWidth(32)) rom_1 ();  // open: addr, data, sel
  ROM #(.addrWidth(6), .dataWidth(32)) rom_2 ();  // open: addr, data, sel
  not not_3 (not_3_out, s_r_ff_3_q);
  Decoder #(.select(5)) decoder_2 (
    .out0(decoder_2_out0[0]), .out1(decoder_2_out0[1]), .out2(decoder_2_out0[2]), .out3(decoder_2_out0[3]),
    .out4(decoder_2_out0[4]), .out5(decoder_2_out0[5]), .out6(decoder_2_out0[6]), .out7(decoder_2_out0[7]),
    .out8(decoder_2_out0[8]), .out9(decoder_2_out0[9]), .out10(decoder_2_out0[10]),
    .out11(decoder_2_out0[11]), .out12(decoder_2_out0[12]), .out13(decoder_2_out0[13]),
    .out14(decoder_2_out0[14]), .out15(decoder_2_out0[15]), .out16(decoder_2_out0[16]),
    .out17(decoder_2_out0[17]), .out18(decoder_2_out0[18]), .out19(decoder_2_out0[19]),
    .out20(decoder_2_out0[20]), .out21(decoder_2_out0[21]), .out22(decoder_2_out0[22]),
    .out23(decoder_2_out0[23]), .out24(decoder_2_out0[24]), .out25(decoder_2_out0[25]),
    .out26(decoder_2_out0[26]), .out27(decoder_2_out0[27]), .out28(decoder_2_out0[28]),
    .out29(decoder_2_out0[29]), .out30(decoder_2_out0[30]), .out31(decoder_2_out0[31]), .sel(counter_2_q[4:0]));  // open: en
  Multiplexer multiplexer_6 (.in0(state), .in1(1'b1), .out(multiplexer_6_out), .sel(s_r_ff_3_q));  // open: en
  not not_4 (not_4_out, s_r_ff_3_q);
  RAM #(.addrWidth(6), .dataWidth(32), .bus("separate")) ram_1 (
    .addr(multiplexer_5_out), .din(or_2_out), .data(ram_1_data), .str(multiplexer_1_out),
    .sel(multiplexer_3_out), .clk(clk), .ld(multiplexer_6_out), .clr(or_1_out));
  RAM #(.addrWidth(6), .dataWidth(32), .bus("separate")) ram_2 (
    .addr(counter_2_q), .din(ram_1_data), .data(ram_2_data), .str(s_r_ff_3_q), .clk(clk), .ld(not_4_out));  // open: sel, clr
  not not_5 (not_5_out, s_r_ff_3_q);
  RAM #(.addrWidth(6), .dataWidth(32), .bus("separate")) ram_3 (
    .addr(multiplexer_5_out), .din(or_2_out), .data(ram_3_data), .str(multiplexer_1_out),
    .sel(multiplexer_2_out), .clk(clk), .ld(multiplexer_6_out), .clr(or_1_out));
  RAM #(.addrWidth(6), .dataWidth(32), .bus("separate")) ram_4 (
    .addr(counter_2_q), .din(ram_3_data), .data(ram_4_data), .str(s_r_ff_3_q), .clk(clk), .ld(not_5_out));  // open: sel, clr
  Multiplexer #(.width(32)) multiplexer_7 (
    .in0(ram_4_data), .in1(ram_3_data), .out(multiplexer_7_out), .sel(s_r_ff_3_q));  // open: en
  Multiplexer #(.width(32)) multiplexer_8 (
    .in0(ram_2_data), .in1(ram_1_data), .out(multiplexer_8_out), .sel(s_r_ff_3_q));  // open: en
  not not_6 (not_6_out, counter_2_q[5]);
  Register #(.width(32)) register_3 (.D(multiplexer_7_out), .en(not_6_out), .Q(x22), .clk(clk), .clr(counter_2_q[5]));
  Register #(.width(32)) register_4 (.D(multiplexer_7_out), .en(counter_2_q[5]), .Q(x21), .clk(clk), .clr(not_6_out));
  Register #(.width(32)) register_5 (.D(decoder_2_out0), .en(not_6_out), .Q(y12), .clk(clk), .clr(counter_2_q[5]));
  Register #(.width(32)) register_6 (.D(decoder_2_out0), .en(counter_2_q[5]), .Q(y11), .clk(clk), .clr(not_6_out));
  Register #(.width(32)) register_7 (.D(multiplexer_8_out), .en(not_6_out), .Q(x12), .clk(clk), .clr(counter_2_q[5]));
  Register #(.width(32)) register_8 (.D(multiplexer_8_out), .en(counter_2_q[5]), .Q(x11), .clk(clk), .clr(not_6_out));
  Register #(.width(32)) register_9 (.D(decoder_2_out0), .en(not_6_out), .Q(y22), .clk(clk), .clr(counter_2_q[5]));
  Register #(.width(32)) register_10 (.D(decoder_2_out0), .en(counter_2_q[5]), .Q(y21), .clk(clk), .clr(not_6_out));

  // Notes on the sheet:
  //   y21: pull=down
  //   x21: pull=down
  //   clear: pull=down
  //   y12: pull=down
  //   y: pull=down
  //   update_frame: pull=down
  //   y11: pull=down
  //   x11: pull=down
  //   y22: pull=down
  //   clk: pull=down
  //   x12: pull=down
  //   state: pull=down
  //   x: pull=down
  //   x22: pull=down
  //   contents of rom_1 (hex, n*v repeats v):
  //   ffffffff fffffff ffffff fffff ffff fff ff f 24*0 f ff fff ffff fffff ffffff fffffff ffffffff
  //   contents of rom_2 (hex, n*v repeats v):
  //   11111111 1111111 111111 11111 1111 111 11 1 24*0 1 11 111 1111 11111 111111 1111111 11111111
endmodule

module int_to_fp (
  input  [31:0] in,
  output [31:0] out
);

  Shifter #(.width(32)) shifter_1 (.in(in), .\dist (5'b10000), .out(out));

  // Notes on the sheet:
  //   in: pull=down
  //   out: pull=down
endmodule

module rising_edge_detector (
);

  wire undriven;

  S_R_Flip_Flop s_r_ff_1 (.S(undriven));  // open: clk, R, Q, Qn, preset, reset, en
endmodule
